// Logisim project 7-segment-display-driver.circ as structural Verilog: 1 circuit, main circuit main
module main (
  input  D,
  input  C,
  input  B,
  input  A,
  output a_2,
  output b_2,
  output c_2,
  output d_2,
  output e,
  output f,
  output g
);

  wire and_1_out, and_2_out, and_3_out, and_4_out, and_5_out, nand_1_out, nand_2_out, nand_3_out, nand_4_out,
       nand_5_out, nand_6_out, nand_7_out, nand_8_out, nand_9_out, nand_10_out, nand_11_out, nand_12_out,
       nand_13_out, nand_14_out, nand_15_out, nand_16_out, nand_17_out, nand_18_out, nand_19_out,
       nand_20_out, nand_21_out, nand_22_out, nand_23_out, nand_24_out, nand_25_out, nand_26_out,
       nand_27_out, nand_28_out, nand_29_out, nand_30_out, nand_31_out, nand_32_out, nand_33_out,
       nand_34_out, nand_35_out, nand_36_out, nand_37_out, nand_38_out, nand_39_out, nand_40_out,
       nand_41_out, nand_42_out, nand_43_out, nand_44_out, nand_45_out, nand_46_out, nand_47_out,
       nand_48_out, nand_49_out, nand_50_out, nand_51_out, nand_52_out, nand_53_out, nand_54_out,
       nand_55_out, nand_56_out, nand_57_out, nand_58_out, nand_59_out, nand_60_out, nand_61_out,
       nand_62_out, nand_63_out, nand_64_out, nand_65_out, nand_66_out, nand_67_out, nand_68_out,
       nand_69_out, nand_70_out, nand_71_out, nand_72_out, nand_73_out, nand_74_out, nand_75_out,
       nand_76_out, nand_77_out, nand_78_out, nand_79_out, nand_80_out, nand_81_out, nand_82_out,
       nand_83_out, nand_85_out, nand_86_out, nand_87_out, nand_88_out, nand_89_out, nand_90_out,
       nand_91_out, nand_92_out, nand_93_out, nand_94_out, nand_95_out, nand_96_out, nand_97_out,
       nand_98_out, nand_99_out, nand_100_out, nand_101_out, nand_102_out, nand_103_out, nand_104_out,
       nand_105_out, nand_106_out, nand_107_out, nand_108_out, nand_109_out, nand_111_out, nand_112_out,
       nand_114_out, nand_115_out, nand_116_out, nand_117_out, nand_118_out, nand_119_out, not_1_out,
       not_2_out, not_3_out, not_4_out, not_5_out, not_6_out, not_7_out, not_8_out, not_9_out, not_10_out,
       not_11_out;

  nand nand_1 (nand_1_out, C, C);
  nand nand_2 (nand_2_out, D, D);
  nand nand_3 (nand_3_out, B, B);
  nand nand_4 (nand_4_out, D, D);
  nand nand_5 (nand_5_out, B, B);
  nand nand_6 (nand_6_out, D, D);
  not not_1 (not_1_out, B);
  not not_2 (not_2_out, B);
  not not_3 (not_3_out, C);
  not not_4 (not_4_out, C);
  nand nand_7 (nand_7_out, C, C);
  nand nand_8 (nand_8_out, A, A);
  nand nand_9 (nand_9_out, A, A);
  nand nand_10 (nand_10_out, D, D);
  nand nand_11 (nand_11_out, C, C);
  nand nand_12 (nand_12_out, A, A);
  nand nand_13 (nand_13_out, D, D);
  nand nand_14 (nand_14_out, D, nand_1_out);
  nand nand_15 (nand_15_out, nand_2_out, nand_3_out);
  nand nand_16 (nand_16_out, nand_4_out, nand_5_out);
  nand nand_17 (nand_17_out, nand_6_out, A);
  not not_5 (not_5_out, D);
  not not_6 (not_6_out, C);
  not not_7 (not_7_out, D);
  not not_8 (not_8_out, D);
  not not_9 (not_9_out, A);
  not not_10 (not_10_out, D);
  not not_11 (not_11_out, A);
  nand nand_18 (nand_18_out, nand_7_out, nand_8_out);
  nand nand_19 (nand_19_out, B, nand_9_out);
  nand nand_20 (nand_20_out, D, B);
  nand nand_21 (nand_21_out, D, C);
  nand nand_22 (nand_22_out, nand_10_out, C);
  nand nand_23 (nand_23_out, nand_11_out, B);
  nand nand_24 (nand_24_out, B, nand_12_out);
  nand nand_25 (nand_25_out, nand_13_out, C);
  nand nand_26 (nand_26_out, C, C);
  nand nand_27 (nand_27_out, A, A);
  nand nand_28 (nand_28_out, D, D);
  nand nand_29 (nand_29_out, D, D);
  nand nand_30 (nand_30_out, nand_14_out, nand_14_out);
  nand nand_31 (nand_31_out, B, B);
  nand nand_32 (nand_32_out, D, D);
  nand nand_33 (nand_33_out, C, C);
  nand nand_34 (nand_34_out, nand_15_out, nand_15_out);
  nand nand_35 (nand_35_out, A, A);
  nand nand_36 (nand_36_out, D, D);
  nand nand_37 (nand_37_out, B, B);
  nand nand_38 (nand_38_out, nand_16_out, nand_17_out);
  nand nand_39 (nand_39_out, B, B);
  nand nand_40 (nand_40_out, D, D);
  nand nand_41 (nand_41_out, C, C);
  and and_1 (and_1_out, not_5_out, C, not_1_out, A);
  and and_2 (and_2_out, D, not_6_out, not_2_out);
  and and_3 (and_3_out, not_7_out, not_3_out, B);
  and and_4 (and_4_out, not_8_out, B, not_9_out);
  and and_5 (and_5_out, not_10_out, not_4_out, not_11_out);
  nand nand_42 (nand_42_out, nand_18_out, nand_19_out);
  nand nand_43 (nand_43_out, nand_20_out, nand_21_out);
  nand nand_44 (nand_44_out, B, B);
  nand nand_45 (nand_45_out, A, A);
  nand nand_46 (nand_46_out, nand_22_out, nand_22_out);
  nand nand_47 (nand_47_out, B, B);
  nand nand_48 (nand_48_out, nand_23_out, nand_24_out);
  nand nand_49 (nand_49_out, nand_25_out, nand_25_out);
  nand nand_50 (nand_50_out, B, B);
  nand nand_51 (nand_51_out, C, C);
  nand nand_52 (nand_52_out, nand_26_out, nand_27_out);
  nand nand_53 (nand_53_out, nand_28_out, B);
  nand nand_54 (nand_54_out, nand_29_out, C);
  nand nand_55 (nand_55_out, C, B);
  nand nand_56 (nand_56_out, nand_30_out, nand_31_out);
  nand nand_57 (nand_57_out, nand_32_out, nand_33_out);
  nand nand_58 (nand_58_out, nand_34_out, nand_35_out);
  nand nand_59 (nand_59_out, nand_36_out, B);
  nand nand_60 (nand_60_out, D, nand_37_out);
  nand nand_61 (nand_61_out, nand_38_out, nand_38_out);
  nand nand_62 (nand_62_out, nand_39_out, A);
  nand nand_63 (nand_63_out, nand_40_out, C);
  nand nand_64 (nand_64_out, D, nand_41_out);
  nand nand_65 (nand_65_out, nand_42_out, nand_42_out);
  nand nand_66 (nand_66_out, nand_43_out, nand_43_out);
  nand nand_67 (nand_67_out, nand_44_out, nand_45_out);
  nand nand_68 (nand_68_out, nand_46_out, nand_47_out);
  nand nand_69 (nand_69_out, nand_48_out, nand_48_out);
  nand nand_70 (nand_70_out, nand_49_out, nand_50_out);
  nand nand_71 (nand_71_out, D, nand_51_out);
  nand nand_72 (nand_72_out, D, A);
  nand nand_73 (nand_73_out, nand_52_out, nand_53_out);
  nand nand_74 (nand_74_out, nand_54_out, nand_54_out);
  nand nand_75 (nand_75_out, nand_55_out, nand_56_out);
  nand nand_76 (nand_76_out, A, A);
  nand nand_77 (nand_77_out, nand_57_out, nand_58_out);
  nand nand_78 (nand_78_out, C, C);
  nand nand_79 (nand_79_out, A, A);
  nand nand_80 (nand_80_out, nand_59_out, nand_59_out);
  nand nand_81 (nand_81_out, nand_60_out, nand_60_out);
  nand nand_82 (nand_82_out, nand_61_out, nand_62_out);
  nand nand_83 (nand_83_out, nand_63_out, nand_64_out);
  nand nand_84 (e, nand_65_out, nand_66_out);
  nand nand_85 (nand_85_out, nand_67_out, nand_68_out);
  nand nand_86 (nand_86_out, A, A);
  nand nand_87 (nand_87_out, C, C);
  nand nand_88 (nand_88_out, nand_69_out, nand_70_out);
  nand nand_89 (nand_89_out, nand_71_out, nand_72_out);
  nand nand_90 (nand_90_out, nand_73_out, nand_73_out);
  nand nand_91 (nand_91_out, nand_74_out, A);
  nand nand_92 (nand_92_out, nand_75_out, nand_75_out);
  nand nand_93 (nand_93_out, D, nand_76_out);
  nand nand_94 (nand_94_out, nand_77_out, nand_77_out);
  nand nand_95 (nand_95_out, nand_78_out, nand_79_out);
  nand nand_96 (nand_96_out, nand_80_out, A);
  nand nand_97 (nand_97_out, nand_81_out, A);
  nand nand_98 (nand_98_out, nand_82_out, nand_82_out);
  nand nand_99 (nand_99_out, nand_83_out, nand_83_out);
  or or_1 (d_2, and_1_out, and_2_out, and_3_out, and_4_out, and_5_out);
  nand nand_100 (nand_100_out, nand_85_out, nand_85_out);
  nand nand_101 (nand_101_out, C, nand_86_out);
  nand nand_102 (nand_102_out, D, nand_87_out);
  nand nand_103 (nand_103_out, D, B);
  nand nand_104 (nand_104_out, nand_88_out, nand_88_out);
  nand nand_105 (nand_105_out, nand_89_out, nand_89_out);
  nand nand_106 (nand_106_out, nand_90_out, nand_91_out);
  nand nand_107 (nand_107_out, nand_92_out, nand_93_out);
  nand nand_108 (nand_108_out, nand_94_out, nand_95_out);
  nand nand_109 (nand_109_out, nand_96_out, nand_97_out);
  nand nand_110 (c_2, nand_98_out, nand_99_out);
  nand nand_111 (nand_111_out, nand_100_out, nand_101_out);
  nand nand_112 (nand_112_out, nand_102_out, nand_103_out);
  nand nand_113 (g, nand_104_out, nand_105_out);
  nand nand_114 (nand_114_out, nand_106_out, nand_106_out);
  nand nand_115 (nand_115_out, nand_107_out, nand_107_out);
  nand nand_116 (nand_116_out, nand_108_out, nand_108_out);
  nand nand_117 (nand_117_out, nand_109_out, nand_109_out);
  nand nand_118 (nand_118_out, nand_111_out, nand_111_out);
  nand nand_119 (nand_119_out, nand_112_out, nand_112_out);
  nand nand_120 (a_2, nand_114_out, nand_115_out);
  nand nand_121 (b_2, nand_116_out, nand_117_out);
  nand nand_122 (f, nand_118_out, nand_119_out);

  // Notes on the sheet:
  //   Visit: http://github.com/marceloboeira for more examples
endmodule
