// Logisim project Addition&Subtraction_Logic_Project_Final_Version_4Bit_Adder.circ as structural Verilog: 3 circuits, main circuit Adder/Subtractor
module _2_s_Complement (
  input  AS,
  input  A0,
  input  A1,
  input  A2,
  output Sign,
  output _2_s_Complement_of_A0,
  output _2_s_Complement_of_A1,
  output _2_s_Complement_of_A2
);

  wire or_1_out, xor_1_out, xor_2_out, xor_3_out;

  or or_1 (or_1_out, A0, A1, A2);
  xor xor_1 (xor_1_out, A0, AS);
  xor xor_2 (xor_2_out, A1, AS);
  xor xor_3 (xor_3_out, A2, AS);
  _4_bit_FA u_4_bit_fa_1 (
    .A0(AS), .B0(xor_1_out), .A1(1'b0), .B1(xor_2_out), .A2(1'b0), .B2(xor_3_out),
    .S0(_2_s_Complement_of_A0), .S1(_2_s_Complement_of_A1), .S2(_2_s_Complement_of_A2));  // open: A3, B3, Cin, Cout, S3
  and and_1 (Sign, AS, or_1_out);

  // Notes on the sheet:
  //   Number Form : 
  //   Sign - A2 - A1 - A0
endmodule

module Adder_Subtractor (
  input  Operation,
  input  AS,
  input  A1,
  input  A2,
  input  BS,
  input  B1,
  input  B2,
  output _1,
  output _2,
  output _3,
  output _4,
  output Zero
);

  wire _2_s_2__2_s_complement_of_a0, _2_s_2__2_s_complement_of_a1, _2_s_2__2_s_complement_of_a2, _2_s_2_sign,
       _2_s__2_s_complement_of_a0, _2_s__2_s_complement_of_a1, _2_s__2_s_complement_of_a2, _2_s_sign,
       main_1_a_2, main_1_b_2, main_1_c_2, main_1_d_2, main_1_e, main_1_f, main_1_g, n4_bit_fa_1_s0,
       n4_bit_fa_1_s1, n4_bit_fa_1_s2, n4_bit_fa_1_s3, xor_1_out;

  xor xor_1 (xor_1_out, BS, Operation);
  _2_s_Complement _2_s (
    .AS(AS), .A0(A1), .A1(A2), .A2(1'b0), .Sign(_2_s_sign),
    ._2_s_Complement_of_A0(_2_s__2_s_complement_of_a0), ._2_s_Complement_of_A1(_2_s__2_s_complement_of_a1),
    ._2_s_Complement_of_A2(_2_s__2_s_complement_of_a2));
  _2_s_Complement _2_s_2 (
    .AS(xor_1_out), .A0(B1), .A1(B2), .A2(1'b0), .Sign(_2_s_2_sign),
    ._2_s_Complement_of_A0(_2_s_2__2_s_complement_of_a0),
    ._2_s_Complement_of_A1(_2_s_2__2_s_complement_of_a1), ._2_s_Complement_of_A2(_2_s_2__2_s_complement_of_a2));
  _4_bit_FA u_4_bit_fa_1 (
    .A0(_2_s__2_s_complement_of_a0), .B0(_2_s_2__2_s_complement_of_a0), .A1(_2_s__2_s_complement_of_a1),
    .B1(_2_s_2__2_s_complement_of_a1), .A2(_2_s__2_s_complement_of_a2), .B2(_2_s_2__2_s_complement_of_a2),
    .A3(_2_s_sign), .B3(_2_s_2_sign), .Cin(1'b0), .S0(n4_bit_fa_1_s0), .S1(n4_bit_fa_1_s1),
    .S2(n4_bit_fa_1_s2), .S3(n4_bit_fa_1_s3));  // open: Cout
  _2_s_Complement _2_s_3 (
    .AS(n4_bit_fa_1_s3), .A0(n4_bit_fa_1_s0), .A1(n4_bit_fa_1_s1), .A2(n4_bit_fa_1_s2), .Sign(_1),
    ._2_s_Complement_of_A0(_2), ._2_s_Complement_of_A1(_3), ._2_s_Complement_of_A2(_4));
  _7_segment_display_driver_main main_1 (
    .D(1'b0), .C(_4), .B(_3), .A(_2), .a_2(main_1_a_2), .b_2(main_1_b_2), .c_2(main_1_c_2), .d_2(main_1_d_2),
    .e(main_1_e), .f(main_1_f), .g(main_1_g));
  nor nor_1 (Zero, _1, _4, _3, _2);
  LED Negative (.in(_1));
  _7_Segment_Display u_7_segment_display_1 (.g(_1));  // open: f, a, b, e, d, c, dp
  LED u_Zero (.in(Zero));
  LED Div__by_Zero (.in(1'b0));
  _7_Segment_Display u_7_segment_display_2 (
    .g(main_1_g), .f(main_1_f), .a(main_1_a_2), .b(main_1_b_2), .e(main_1_e), .d(main_1_d_2), .c(main_1_c_2));  // open: dp

  // Notes on the sheet:
  //   Number Form : 
  //   Sign - N2 -  N1
  //   7-Segment-Decoder
  //   Result
endmodule

module _4_bit_FA (
  input  Cin,
  input  A0,
  input  B0,
  input  A1,
  input  B1,
  input  A2,
  input  B2,
  input  A3,
  input  B3,
  output S0,
  output S1,
  output S2,
  output S3,
  output Cout
);

  wire adder_1_cout, adder_2_cout, adder_3_cout;

  Adder #(.width(1)) adder_1 (.a(A0), .b(B0), .out(S0), .cin(Cin), .cout(adder_1_cout));
  Adder #(.width(1)) adder_2 (.a(A1), .b(B1), .out(S1), .cin(adder_1_cout), .cout(adder_2_cout));
  Adder #(.width(1)) adder_3 (.a(A2), .b(B2), .out(S2), .cin(adder_2_cout), .cout(adder_3_cout));
  Adder #(.width(1)) adder_4 (.a(A3), .b(B3), .out(S3), .cin(adder_3_cout), .cout(Cout));
endmodule
