// Logisim project Integration_Logic_Project_Final_Version.circ as structural Verilog: 1 circuit, main circuit Arithmetic Logic Unit (ALU)
module Arithmetic_Logic_Unit__ALU (
  input  As,
  input  A2,
  input  A1,
  input  Bs,
  input  B2,
  input  B1,
  input  SW1,
  input  Sw2
);

  wire adder_subtractor_1__1, adder_subtractor_1__2, adder_subtractor_1__3, adder_subtractor_1__4,
       adder_subtractor_1_zero, and_1_out, and_2_out, buffer_1_out, main_1_a_2, main_1_b_2, main_1_c_2,
       main_1_d_2, main_1_e, main_1_f, main_1_g, multiplexer_1_out, multiplexer_2_out, multiplexer_3_out,
       multiplexer_4_out, multiplexer_5_out, multiplexer_6_out, multiplexer_7_out, multiplication_1__1,
       multiplication_1__2, multiplication_1__3, multiplication_1__4, multiplication_1_negative,
       multiplication_1_zero, not_1_out, not_2_out, or_1_out, reminder_1_div_by_zero,
       reminder_1_first_bit_of_output, reminder_1_negative, reminder_1_second_bit_of_output, reminder_1_zero;

  Reminder reminder_1 (
    .AS(As), .A2(A2), .A1(A1), .BS(Bs), .B2(B2), .B1(B1),
    .First_BIT_of_output(reminder_1_first_bit_of_output),
    .Second_BIT_of_output(reminder_1_second_bit_of_output), .Div_by_Zero(reminder_1_div_by_zero),
    .Zero(reminder_1_zero), .Negative(reminder_1_negative));
  Multiplication multiplication_1 (
    .AS(As), .A2(A2), .A1(A1), .BS(Bs), .B2(B2), .B1(B1), ._1(multiplication_1__1),
    .Zero(multiplication_1_zero), ._2(multiplication_1__2), ._3(multiplication_1__3),
    ._4(multiplication_1__4), .Negative(multiplication_1_negative));
  Adder_Subtractor adder_subtractor_1 (
    .Operation(Sw2), .AS(As), .A1(A1), .A2(A2), .BS(Bs), .B1(B1), .B2(B2), ._1(adder_subtractor_1__1),
    ._2(adder_subtractor_1__2), ._3(adder_subtractor_1__3), ._4(adder_subtractor_1__4),
    .Zero(adder_subtractor_1_zero));
  Multiplexer #(.select(2)) multiplexer_1 (
    .in0(adder_subtractor_1__2), .in1(adder_subtractor_1__2), .in2(multiplication_1__1),
    .in3(reminder_1_first_bit_of_output), .out(multiplexer_1_out), .sel({SW1, Sw2}));  // open: en
  Multiplexer #(.select(2)) multiplexer_2 (
    .in0(adder_subtractor_1__3), .in1(adder_subtractor_1__3), .in2(multiplication_1__2),
    .in3(reminder_1_second_bit_of_output), .out(multiplexer_2_out), .sel({SW1, Sw2}));  // open: en
  Multiplexer #(.select(2)) multiplexer_3 (
    .in0(adder_subtractor_1__4), .in1(adder_subtractor_1__4), .in2(multiplication_1__3), .in3(1'b0),
    .out(multiplexer_3_out), .sel({SW1, Sw2}));  // open: en
  Multiplexer #(.select(2)) multiplexer_4 (
    .in0(1'b0), .in1(1'b0), .in2(multiplication_1__4), .in3(1'b0), .out(multiplexer_4_out), .sel({SW1, Sw2}));  // open: en
  Multiplexer #(.select(2)) multiplexer_5 (
    .in0(1'b0), .in1(1'b0), .in2(1'b0), .in3(reminder_1_div_by_zero), .out(multiplexer_5_out),
    .sel({SW1, Sw2}));  // open: en
  Multiplexer #(.select(2)) multiplexer_6 (
    .in0(adder_subtractor_1_zero), .in1(adder_subtractor_1_zero), .in2(multiplication_1_zero),
    .in3(reminder_1_zero), .out(multiplexer_6_out), .sel({SW1, Sw2}));  // open: en
  Multiplexer #(.select(2)) multiplexer_7 (
    .in0(adder_subtractor_1__1), .in1(adder_subtractor_1__1), .in2(multiplication_1_negative),
    .in3(reminder_1_negative), .out(multiplexer_7_out), .sel({SW1, Sw2}));  // open: en
  buf buffer_1 (buffer_1_out, multiplexer_5_out);
  or or_1 (or_1_out, multiplexer_5_out, multiplexer_1_out);
  _7_segment_display_driver_main main_1 (
    .D(multiplexer_4_out), .C(multiplexer_3_out), .B(multiplexer_2_out), .A(or_1_out), .a_2(main_1_a_2),
    .b_2(main_1_b_2), .c_2(main_1_c_2), .d_2(main_1_d_2), .e(main_1_e), .f(main_1_f), .g(main_1_g));
  // Simple_buzzer simple_buzzer_1: pin names not known; wires that end beside it: buffer_1_out, 1'b0
  LED Zero (.in(multiplexer_6_out));
  LED Negative (.in(multiplexer_7_out));
  not not_1 (not_1_out, multiplexer_5_out);
  _7_Segment_Display u_7_segment_display_1 (.g(multiplexer_7_out));  // open: f, a, b, e, d, c, dp
  not not_2 (not_2_out, multiplexer_5_out);
  and and_1 (and_1_out, not_1_out, main_1_b_2);
  _7_Segment_Display u_7_segment_display_2 (
    .g(main_1_g), .f(main_1_f), .a(main_1_a_2), .b(and_1_out), .e(main_1_e), .d(main_1_d_2), .c(and_2_out));  // open: dp
  and and_2 (and_2_out, not_2_out, main_1_c_2);

  // Notes on the sheet:
  //   Remainder Circuit
  //   Multiplication Circuit
  //   Addition/Subtraction Circuit
  //   Form of input Numbers:
  //   As A2 A1
  //   Bs B2 B1
  //   Form of Operation:
  //   Sw2 Sw1
  //   7-Segment-Decoder
  //   Operations:
  //   ADD: 0 0
  //   Multiplication: 0 1
  //   Subtraction: 1 0
  //   Remainder: 1 1
  //   Div by zero Buzzer
  //   Result
endmodule
