// Logisim project Multiplication_Logic_Project_Final_Version.circ as structural Verilog: 2 circuits, main circuit Multiplication
module Multiplication (
  input  AS,
  input  A2,
  input  A1,
  input  BS,
  input  B2,
  input  B1,
  output _1,
  output Zero,
  output _2,
  output _3,
  output _4,
  output Negative
);

  wire and_1_out, and_2_out, and_3_out, half_adder_1_carry, main_1_a_2, main_1_b_2, main_1_c_2, main_1_d_2,
       main_1_e, main_1_f, main_1_g, not_1_out, not_2_out, not_3_out, or_1_out, or_2_out, xor_1_out;

  and and_1 (and_1_out, A1, B2);
  and and_2 (and_2_out, B1, A2);
  and and_3 (and_3_out, A2, B2);
  xor xor_1 (xor_1_out, BS, AS);
  and and_4 (_1, A1, B1);
  HALF_ADDER half_adder_1 (.A(and_1_out), .B(and_2_out), .SUM(_2), .CARRY(half_adder_1_carry));
  HALF_ADDER half_adder_2 (.A(half_adder_1_carry), .B(and_3_out), .SUM(_3), .CARRY(_4));
  _7_segment_display_driver_main main_1 (
    .D(_4), .C(_3), .B(_2), .A(_1), .a_2(main_1_a_2), .b_2(main_1_b_2), .c_2(main_1_c_2), .d_2(main_1_d_2),
    .e(main_1_e), .f(main_1_f), .g(main_1_g));
  or or_1 (or_1_out, _1, _2);
  not not_1 (not_1_out, or_1_out);
  or or_2 (or_2_out, _3, _4);
  and and_5 (Zero, not_1_out, not_2_out);
  not not_2 (not_2_out, or_2_out);
  not not_3 (not_3_out, Zero);
  and and_6 (Negative, xor_1_out, not_3_out);
  _7_Segment_Display u_7_segment_display_1 (.g(Negative));  // open: f, a, b, e, d, c, dp
  _7_Segment_Display u_7_segment_display_2 (
    .g(main_1_g), .f(main_1_f), .a(main_1_a_2), .b(main_1_b_2), .e(main_1_e), .d(main_1_d_2), .c(main_1_c_2));  // open: dp
  LED u_Zero (.in(Zero));
  LED u_Negative (.in(Negative));
  LED Div__by_Zero (.in(1'b0));

  // Notes on the sheet:
  //   7-Segment-Decoder
  //   Result
endmodule

module HALF_ADDER (
  input  A,
  input  B,
  output SUM,
  output CARRY
);

  xor xor_1 (SUM, A, B);
  and and_1 (CARRY, A, B);
endmodule
