// Logisim project Reminder_Logic_Project_Final_Version.circ as structural Verilog: 1 circuit, main circuit Reminder
module Reminder (
  input  AS,
  input  A2,
  input  A1,
  input  BS,
  input  B2,
  input  B1,
  output First_BIT_of_output,
  output Second_BIT_of_output,
  output Div_by_Zero,
  output Zero,
  output Negative
);

  wire and_1_out, and_2_out, and_3_out, and_4_out, and_9_out, and_10_out, main_1_a_2, main_1_b_2, main_1_c_2,
       main_1_d_2, main_1_e, main_1_f, main_1_g, not_1_out, not_2_out, not_4_out, not_5_out, not_6_out,
       not_7_out, not_8_out, or_1_out, or_2_out, or_3_out;

  not not_1 (not_1_out, A1);
  and and_1 (and_1_out, A2, B1);
  and and_2 (and_2_out, A1, B2);
  or or_1 (or_1_out, B1, B2);
  not not_2 (not_2_out, and_1_out);
  and and_3 (and_3_out, B1, B2);
  and and_4 (and_4_out, not_1_out, A2);
  not not_3 (Div_by_Zero, or_1_out);
  and and_5 (First_BIT_of_output, not_2_out, and_2_out);
  and and_6 (Second_BIT_of_output, and_3_out, and_4_out);
  or or_2 (or_2_out, First_BIT_of_output, Second_BIT_of_output);
  not not_4 (not_4_out, Div_by_Zero);
  not not_5 (not_5_out, or_2_out);
  or or_3 (or_3_out, First_BIT_of_output, Div_by_Zero);
  and and_7 (Zero, not_4_out, not_5_out);
  _7_segment_display_driver_main main_1 (
    .D(1'b0), .C(1'b0), .B(Second_BIT_of_output), .A(or_3_out), .a_2(main_1_a_2), .b_2(main_1_b_2),
    .c_2(main_1_c_2), .d_2(main_1_d_2), .e(main_1_e), .f(main_1_f), .g(main_1_g));
  not not_6 (not_6_out, not_5_out);
  and and_8 (Negative, not_6_out, AS);
  not not_7 (not_7_out, Div_by_Zero);
  not not_8 (not_8_out, Div_by_Zero);
  and and_9 (and_9_out, not_7_out, main_1_b_2);
  _7_Segment_Display u_7_segment_display_1 (
    .g(main_1_g), .f(main_1_f), .a(main_1_a_2), .b(and_9_out), .e(main_1_e), .d(main_1_d_2), .c(and_10_out));  // open: dp
  _7_Segment_Display u_7_segment_display_2 (.g(Negative));  // open: f, a, b, e, d, c, dp
  and and_10 (and_10_out, main_1_c_2, not_8_out);
  LED u_Div_by_Zero (.in(Div_by_Zero));
  LED u_Zero (.in(Zero));
  LED u_Negative (.in(Negative));

  // Notes on the sheet:
  //   7-Segment-Decoder
  //   Result
endmodule
